# Fritzing sketch clock (saved by Fritzing 0.7.11b)
breadboards: 1

parts:
  J1 = Basic Servo
  Arduino1 = Arduino

nets:
  GND: J1.gnd, Arduino1.GND
  VCC: J1.vcc, Arduino1.+5V
  N1: J1.pulse, Arduino1.D11
